# Fritzing sketch Transmitter (saved by Fritzing 0.9.3b)

parts:
  Componente1 = Arduino Nano (Rev3.0)
  Componente2 = Thumb Joystick
  Componente3 = Thumb Joystick
  Componente4 = NRF24L01+ Breakout Board
  BAT1 = BC9VPC [package=bc9vpc]

nets:
  GND: Componente1.GND, Componente4.GND, BAT1.V-
  N1: Componente1.D5, Componente3.SEL
  N2: Componente1.D6, Componente2.SEL
  N3: Componente1.D9, Componente4.CE
  N4: Componente1.D10, Componente4.CS
  N5: Componente1.D11/MOSI, Componente4.MOSI
  N6: Componente1.D12/MISO, Componente4.MISO
  N7: Componente1.VIN, BAT1.V+
  5V: Componente1.5V, Componente4.VCC
  N8: Componente1.A3, Componente3.HORZ
  N9: Componente1.A2, Componente3.VERT
  N10: Componente1.A1, Componente2.HORZ
  N11: Componente1.A0, Componente2.VERT
  N12: Componente1.D13/SCK, Componente4.SCK
